# Fritzing sketch i2c2midi_fritzing (saved by Fritzing 0.9.4)
stripboards: 2

parts:
  Teensy_3_1 = Teensy 3.1
  R4 = Resistor [tolerance=±5% resistance=47 package=THT]
  R1 = Resistor [tolerance=±5% resistance=2.2k package=THT]
  R2 = Resistor [tolerance=±5% resistance=2.2k package=THT]
  R3 = Resistor [tolerance=±5% resistance=47 package=THT]
  J1_(POWER) = female pin header, 5 pins [form="♀ (female)"]
  J2_(I2C_IN) = female pin header, 3 pins [form="♀ (female)"]
  TRS1_(MIDI_OUT) = Audio Jack (TRS) 3.5mm [package="4Ucon 08780 [THT]"]

nets:
  N1: Teensy_3_1.GND, J1_(POWER).pin1, J2_(I2C_IN).pin1, TRS1_(MIDI_OUT).Sleeve
  N2: Teensy_3_1.D1, R3.Pin_1
  N3: Teensy_3_1.A4/D18, R1.Pin_0, J2_(I2C_IN).pin3
  N4: Teensy_3_1.A5/D19, R2.Pin_0, J2_(I2C_IN).pin2
  N5: Teensy_3_1.3V3, R4.Pin_1, R1.Pin_1, R2.Pin_1
  N6: Teensy_3_1.Vin, J1_(POWER).pin3
  N7: R4.Pin_0, TRS1_(MIDI_OUT).Ring
  N8: R3.Pin_0, TRS1_(MIDI_OUT).Tip

custom parts:
  Teensy 3.1: The Teensy is a complete USB-based microcontoller development system, in a very small footprint, capable of implementing many types of projects. All programming is done via the USB port. No special programmer is needed, only a standard micro-USB cable and a PC or Macintosh with a USB port. It has a USB keyboard/mouse/joystick emulation stack and can be programmed through Arduino IDE.
